# Fritzing sketch bstep-ch347f-2txah-evb (saved by Fritzing 1.0.3b)

parts:
  U3 = CH347F (USB to SPI/I2C/JTAG/UART, QFN28) [package=QFN28]
  U4 = TX-AH-R900PNR (Taixin 802.11ah Module) [package=TX-AH-R900PNR]
  U5 = TX-AH-R900PNR (Taixin 802.11ah Module) [package=TX-AH-R900PNR]

nets:
  N1: U3.TXD1, U4.A10
  N2: U3.RXD1, U4.A11
  N3: U3.TXD0, U5.A10
  GND: U3.GND, U4.GND, U5.GND
  N4: U3.RXD0, U5.A11
